# Fritzing sketch Sensor (saved by Fritzing 0.9.3b)
stripboards: 1

parts:
  U1 = ESP8266 WiFi Module [part_number=ESP8266]
  TP1 = TP4056 [chip_label=TP4056 package="DIP (Dual Inline) [THT]"]
  J1 = Dagu DGServo 9g header (male) [package=THT]
  J5 = female pin header, 2 pins [form="♀ (female)"]
  J3 = Camdenboss CTB0158-6 [part_number=CTB0158-6 package=THT]

nets:
  N1: U1.RXD, U1.VCC, TP1.pin5, J5.pin2
  N2: U1.GPIO_0, U1.RST, J5.pin1
  N3: U1.GPIO_2, U1.CH_PD
  N4: U1.GND, U1.TXD
  N5: TP1.pin2, TP1.pin6
  N6: J1.gnd, J3.pin5
  N7: J1.pulse, J3.pin6

custom parts:
  ESP8266 WiFi Module: Generic WiFi Module based on the ESP8266 with onboard PCB antenna and UART communications
  TP4056: A DIP stand-in part for whatever IC you want. With 6 pins on a 300mil dual inline package (DIP) footprint.
